# Fritzing sketch fritzing_diagram (saved by Fritzing 1.0.3b)
breadboards: 1

parts:
  HC-SR04_Sensor_1 = HC-SR04 Ultrasonic Distance Sensor
  MCU1 = Raspberry Pi Zero
  R1 = Resistor [tolerance=±5% resistance=1k package="0603 [SMD]"]
  R2 = Resistor [tolerance=±5% resistance=2.2k package="0603 [SMD]"]

nets:
  N1: HC-SR04_Sensor_1.VCC, MCU1.pin_2, MCU1.pin_4
  N2: HC-SR04_Sensor_1.TRIG, MCU1.pin_16
  N3: HC-SR04_Sensor_1.ECHO, R1.Pin_0
  N4: HC-SR04_Sensor_1.GND, MCU1.pin_6, MCU1.pin_9
  N5: MCU1.pin_18, R2.Pin_1
  N6: R1.Pin_1, R2.Pin_0

notes:
  Ultrasonic Sensor
  VCC : +ve rail
  TRIG: GPIO 16
  ECHO: 1kOhm - 2kOhm - GPIO 18
  GND: -ve rail
